# Fritzing sketch esp32-s2-mini-oled (saved by Fritzing 0.9.4)

parts:
  OLED1 = OLED 128x64 I2C Monochrome Display VDD-GND
  A1 = Wemos S2 Mini [part_number="WeMos D1 Mini Lite"]
  Компонент1 = HC-SR501 Body Sensor Module

nets:
  N1: OLED1.VDD, A1.Pin_8
  GND: OLED1.GND, A1.Pin_18, A1.Pin_26, Компонент1.GND
  N2: OLED1.SCK, A1.Pin_22
  N3: OLED1.SDA, A1.Pin_21
  N4: A1.Pin_16, Компонент1.OUT
  N5: A1.Pin_17, Компонент1.VCC

custom parts:
  OLED 128x64 I2C Monochrome Display VDD-GND: OLED 128x64 I2C Monochrome Display. Note: there are two variants of this part, this one is the VDD GND SCK SDA variant. The other is GND VDD SCK SDA. Make sure you select the part that matches your module as using the incorrect part will probably destroy your module! In addition the mounting holes are marked on silkscreen but not by default drilled. If you want drilled mounting holes, copy a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
  Wemos S2 Mini: A mini wifi board based on the ESP32-S2FN4R2.
  HC-SR501 Body Sensor Module: Pyroelectric Infrared PIR Motion Sensor Detector Module
